// Logisim project CSE332MainProject.circ as structural Verilog: 6 circuits, main circuit AluControl
// ALU CONTROL
module AluControl (
  input  [2:0] \function ,
  input  [1:0] op,
  output Binvert,
  output A,
  output B
);

  wire and_1_out, and_2_out, and_3_out, not_1_out, not_2_out, not_3_out, not_5_out;

  not not_1 (not_1_out, \function [2]);
  not not_2 (not_2_out, op[1]);
  not not_3 (not_3_out, \function [1]);
  not not_4 (A, \function [1]);
  not not_5 (not_5_out, \function [2]);
  and and_1 (and_1_out, not_2_out, op[0]);
  and and_2 (and_2_out, not_1_out, not_3_out, \function [0]);
  and and_3 (and_3_out, not_5_out, \function [1], \function [0]);
  or or_1 (B, and_3_out, \function [2]);
  or or_2 (Binvert, and_1_out, and_2_out, \function [2]);
endmodule

// Control_unit
module controlUnit (
  input  [3:0] in_1,
  output regDest,
  output AluSrc,
  output memToReg,
  output regWrite,
  output memRead,
  output memWrite,
  output Beq,
  output BNE,
  output Jmp,
  output op1,
  output op2
);

  wire and_1_out, and_2_out, and_3_out, and_4_out, and_9_out, not_1_out, not_2_out, not_3_out, not_4_out,
       not_5_out, not_6_out, not_7_out;

  not not_1 (not_1_out, in_1[2]);
  not not_2 (not_2_out, in_1[1]);
  not not_3 (not_3_out, in_1[0]);
  and and_1 (and_1_out, in_1[2], in_1[1]);
  not not_4 (not_4_out, in_1[1]);
  and and_2 (and_2_out, in_1[2], not_4_out);
  and and_3 (and_3_out, in_1[1], in_1[0]);
  not not_5 (not_5_out, in_1[0]);
  and and_4 (and_4_out, in_1[1], not_3_out);
  not not_6 (not_6_out, in_1[1]);
  and and_5 (Jmp, in_1[2], in_1[0]);
  and and_6 (regDest, not_1_out, not_2_out, not_5_out);
  not not_7 (not_7_out, in_1[2]);
  and and_7 (BNE, not_3_out, in_1[2], not_6_out);
  or or_1 (op2, and_2_out, and_3_out);
  and and_8 (memRead, not_2_out, not_1_out, in_1[0]);
  and and_9 (and_9_out, not_1_out, not_2_out);
  and and_10 (memWrite, not_3_out, in_1[1], not_7_out);
  and and_11 (Beq, in_1[1], in_1[0]);
  or or_2 (AluSrc, and_4_out, memRead);
  or or_3 (regWrite, and_9_out, and_1_out);
  or or_4 (op1, Jmp, regDest);

  assign memToReg = memRead;
endmodule

// 16 bit ALU
module _16bit_ALU (
  input  C_in,
  input  [15:0] oparend_A,
  input  [15:0] oparend_B,
  input  [1:0] Operation,
  input  B_invert,
  output [15:0] result,
  output zero,
  output Overflow,
  output Carry15
);

  wire n1bit_alu_1_carry0, n1bit_alu_2_carry0, n1bit_alu_3_carry0, n1bit_alu_4_carry0, n1bit_alu_5_carry0,
       n1bit_alu_6_carry0, n1bit_alu_7_carry0, n1bit_alu_8_carry0, n1bit_alu_9_carry0, n1bit_alu_10_carry0,
       n1bit_alu_11_carry0, n1bit_alu_12_carry0, n1bit_alu_13_carry0, n1bit_alu_14_carry0,
       n1bit_alu_15_carry0;

  _1bit_ALU u_1bit_alu_1 (
    .Result0(result[0]), .Carry0(n1bit_alu_1_carry0), .Operand_B(oparend_B[0]), .Operand_A(oparend_A[0]),
    .Carry_In(C_in), .Binvert(B_invert), .Operation(Operation));
  _1bit_ALU u_1bit_alu_2 (
    .Result0(result[1]), .Carry0(n1bit_alu_2_carry0), .Operand_B(oparend_B[1]), .Operand_A(oparend_A[1]),
    .Carry_In(n1bit_alu_1_carry0), .Binvert(B_invert), .Operation(Operation));
  _1bit_ALU u_1bit_alu_3 (
    .Result0(result[2]), .Carry0(n1bit_alu_3_carry0), .Operand_B(oparend_B[2]), .Operand_A(oparend_A[2]),
    .Carry_In(n1bit_alu_2_carry0), .Binvert(B_invert), .Operation(Operation));
  _1bit_ALU u_1bit_alu_4 (
    .Result0(result[3]), .Carry0(n1bit_alu_4_carry0), .Operand_B(oparend_B[3]), .Operand_A(oparend_A[3]),
    .Carry_In(n1bit_alu_3_carry0), .Binvert(B_invert), .Operation(Operation));
  _1bit_ALU u_1bit_alu_5 (
    .Result0(result[4]), .Carry0(n1bit_alu_5_carry0), .Operand_B(oparend_B[4]), .Operand_A(oparend_A[4]),
    .Carry_In(n1bit_alu_4_carry0), .Binvert(B_invert), .Operation(Operation));
  _1bit_ALU u_1bit_alu_6 (
    .Result0(result[5]), .Carry0(n1bit_alu_6_carry0), .Operand_B(oparend_B[5]), .Operand_A(oparend_A[5]),
    .Carry_In(n1bit_alu_5_carry0), .Binvert(B_invert), .Operation(Operation));
  _1bit_ALU u_1bit_alu_7 (
    .Result0(result[6]), .Carry0(n1bit_alu_7_carry0), .Operand_B(oparend_B[6]), .Operand_A(oparend_A[6]),
    .Carry_In(n1bit_alu_6_carry0), .Binvert(B_invert), .Operation(Operation));
  _1bit_ALU u_1bit_alu_8 (
    .Result0(result[7]), .Carry0(n1bit_alu_8_carry0), .Operand_B(oparend_B[7]), .Operand_A(oparend_A[7]),
    .Carry_In(n1bit_alu_7_carry0), .Binvert(B_invert), .Operation(Operation));
  _1bit_ALU u_1bit_alu_9 (
    .Result0(result[8]), .Carry0(n1bit_alu_9_carry0), .Operand_B(oparend_B[8]), .Operand_A(oparend_A[8]),
    .Carry_In(n1bit_alu_8_carry0), .Binvert(B_invert), .Operation(Operation));
  _1bit_ALU u_1bit_alu_10 (
    .Result0(result[9]), .Carry0(n1bit_alu_10_carry0), .Operand_B(oparend_B[9]), .Operand_A(oparend_A[9]),
    .Carry_In(n1bit_alu_9_carry0), .Binvert(B_invert), .Operation(Operation));
  _1bit_ALU u_1bit_alu_11 (
    .Result0(result[10]), .Carry0(n1bit_alu_11_carry0), .Operand_B(oparend_B[10]), .Operand_A(oparend_A[10]),
    .Carry_In(n1bit_alu_10_carry0), .Binvert(B_invert), .Operation(Operation));
  _1bit_ALU u_1bit_alu_12 (
    .Result0(result[11]), .Carry0(n1bit_alu_12_carry0), .Operand_B(oparend_B[11]), .Operand_A(oparend_A[11]),
    .Carry_In(n1bit_alu_11_carry0), .Binvert(B_invert), .Operation(Operation));
  _1bit_ALU u_1bit_alu_13 (
    .Result0(result[12]), .Carry0(n1bit_alu_13_carry0), .Operand_B(oparend_B[12]), .Operand_A(oparend_A[12]),
    .Carry_In(n1bit_alu_12_carry0), .Binvert(B_invert), .Operation(Operation));
  _1bit_ALU u_1bit_alu_14 (
    .Result0(result[13]), .Carry0(n1bit_alu_14_carry0), .Operand_B(oparend_B[13]), .Operand_A(oparend_A[13]),
    .Carry_In(n1bit_alu_13_carry0), .Binvert(B_invert), .Operation(Operation));
  _1bit_ALU u_1bit_alu_15 (
    .Result0(result[14]), .Carry0(n1bit_alu_15_carry0), .Operand_B(oparend_B[14]), .Operand_A(oparend_A[14]),
    .Carry_In(n1bit_alu_14_carry0), .Binvert(B_invert), .Operation(Operation));
  _1bit_ALU u_1bit_alu_16 (
    .Result0(result[15]), .Carry0(Carry15), .Operand_B(oparend_B[15]), .Operand_A(oparend_A[15]),
    .Carry_In(n1bit_alu_15_carry0), .Binvert(B_invert), .Operation(Operation));
  xor xor_1 (Overflow, n1bit_alu_15_carry0, Carry15);
  nor nor_1 (zero, result[0], result[1], result[2], result[3], result[4], result[5], result[6], result[7], result[8], result[9], result[10], result[11], result[12], result[13], result[14], result[15]);

  // Other names for the same wires on the sheet: A0 = oparend_A[0]; A1 = oparend_A[1]; A2 = oparend_A[2];
  //   A3 = oparend_A[3]; A4 = oparend_A[4]; A5 = oparend_A[5]; A6 = oparend_A[6]; A7 = oparend_A[7];
  //   A8 = oparend_A[8]; A9 = oparend_A[9]; A10 = oparend_A[10]; A11 = oparend_A[11]; A12 = oparend_A[12];
  //   A13 = oparend_A[13]; A14 = oparend_A[14]; A15 = oparend_A[15]; B0 = oparend_B[0]; B1 = oparend_B[1];
  //   B2 = oparend_B[2]; B3 = oparend_B[3]; B4 = oparend_B[4]; B5 = oparend_B[5]; B6 = oparend_B[6];
  //   B7 = oparend_B[7]; B8 = oparend_B[8]; B9 = oparend_B[9]; B10 = oparend_B[10]; B11 = oparend_B[11];
  //   B12 = oparend_B[12]; B13 = oparend_B[13]; B14 = oparend_B[14]; B15 = oparend_B[15]
endmodule

module _1bit_ALU (
  input  Operand_B,
  input  Operand_A,
  input  Carry_In,
  input  Binvert,
  input  [1:0] Operation,
  output Result0,
  output Carry0
);

  wire adder_1_out, and_1_out, multiplexer_1_out, not_1_out, or_1_out;

  not not_1 (not_1_out, Operand_B);
  Multiplexer multiplexer_1 (.in0(Operand_B), .in1(not_1_out), .out(multiplexer_1_out), .sel(Binvert));  // open: en
  and and_1 (and_1_out, Operand_A, multiplexer_1_out);
  or or_1 (or_1_out, Operand_A, multiplexer_1_out);
  Adder #(.width(1)) adder_1 (.a(Operand_A), .b(multiplexer_1_out), .out(adder_1_out), .cin(Carry_In), .cout(Carry0));
  Multiplexer #(.select(2)) multiplexer_2 (
    .in0(and_1_out), .in1(or_1_out), .in2(adder_1_out), .out(Result0), .sel(Operation));  // open: in3, en
endmodule

// 16_Bit_Register
module _16bit_register (
  input  Clock,
  input  [2:0] RS,
  input  [2:0] RT,
  input  [2:0] Write_Register_RD,
  input  [15:0] Write_Data,
  input  Register_Write,
  output [15:0] Read_Data_RS,
  output [15:0] Read_Data_RT
);

  wire and_1_out, and_2_out, and_3_out, and_4_out, and_5_out, and_6_out, and_7_out, and_8_out,
       decoder_1_out0, decoder_1_out1, decoder_1_out2, decoder_1_out3, decoder_1_out4, decoder_1_out5,
       decoder_1_out6, decoder_1_out7;
  wire [15:0] R0_q, R1_q, R2_q, R3_q, R4_q, R5_q, R6_q, R7_q;

  Decoder #(.select(3), .enable("false")) decoder_1 (
    .out0(decoder_1_out0), .out1(decoder_1_out1), .out2(decoder_1_out2), .out3(decoder_1_out3),
    .out4(decoder_1_out4), .out5(decoder_1_out5), .out6(decoder_1_out6), .out7(decoder_1_out7),
    .sel(Write_Register_RD));
  and and_1 (and_1_out, decoder_1_out0, Register_Write);
  and and_2 (and_2_out, decoder_1_out1, Register_Write);
  and and_3 (and_3_out, decoder_1_out2, Register_Write);
  and and_4 (and_4_out, decoder_1_out3, Register_Write);
  and and_5 (and_5_out, Register_Write, decoder_1_out4);
  and and_6 (and_6_out, Register_Write, decoder_1_out5);
  and and_7 (and_7_out, Register_Write, decoder_1_out6);
  and and_8 (and_8_out, Register_Write, decoder_1_out7);
  Register #(.width(16)) R0 (.D(Write_Data), .en(and_1_out), .Q(R0_q), .clk(Clock));  // open: clr
  Register #(.width(16)) R1 (.D(Write_Data), .en(and_2_out), .Q(R1_q), .clk(Clock));  // open: clr
  Register #(.width(16)) R2 (.D(Write_Data), .en(and_3_out), .Q(R2_q), .clk(Clock));  // open: clr
  Register #(.width(16)) R3 (.D(Write_Data), .en(and_4_out), .Q(R3_q), .clk(Clock));  // open: clr
  Register #(.width(16)) R4 (.D(Write_Data), .en(and_5_out), .Q(R4_q), .clk(Clock));  // open: clr
  Register #(.width(16)) R5 (.D(Write_Data), .en(and_6_out), .Q(R5_q), .clk(Clock));  // open: clr
  Register #(.width(16)) R6 (.D(Write_Data), .en(and_7_out), .Q(R6_q), .clk(Clock));  // open: clr
  Register #(.width(16)) R7 (.D(Write_Data), .en(and_8_out), .Q(R7_q), .clk(Clock));  // open: clr
  Multiplexer #(.select(3), .width(16)) multiplexer_1 (
    .in0(R0_q), .in1(R1_q), .in2(R2_q), .in3(R3_q), .in4(R4_q), .in5(R5_q), .in6(R6_q), .in7(R7_q),
    .out(Read_Data_RS), .sel(RS));  // open: en
  Multiplexer #(.select(3), .width(16)) multiplexer_2 (
    .in0(R0_q), .in1(R1_q), .in2(R2_q), .in3(R3_q), .in4(R4_q), .in5(R5_q), .in6(R6_q), .in7(R7_q),
    .out(Read_Data_RT), .sel(RT));  // open: en
endmodule

module Cpu_Main (
  input  carry_in,
  input  in_2,
  output overflow,
  output Carry15
);

  wire alucontrol_1_binvert, and_1_out, and_2_out, clock_1_out, controlunit_1_alusrc, controlunit_1_beq,
       controlunit_1_bne, controlunit_1_jmp, controlunit_1_memread, controlunit_1_memtoreg,
       controlunit_1_memwrite, controlunit_1_regdest, controlunit_1_regwrite, n16bit_alu_1_zero, not_1_out,
       or_1_out;
  wire [1:0] alucontrol_1_b, controlunit_1_op1;
  wire [2:0] multiplexer_1_out;
  wire [15:0] adder_1_out, adder_2_out, bit_extender_1_out, bit_extender_2_out, multiplexer_2_out,
       multiplexer_3_out, multiplexer_4_out, multiplexer_5_out, n16bit_alu_1_result,
       n16bit_register_1_read_data_rs, n16bit_register_1_read_data_rt, ram_1_data, register_1_q, rom_1_data;

  Register #(.width(16)) register_1 (
    .D(multiplexer_4_out), .Q(register_1_q), .clk(clock_1_out), .clr(in_2));  // open: en
  Clock clock_1 (.out(clock_1_out));
  Adder #(.width(16)) adder_1 (.a(16'h4), .b(register_1_q), .out(adder_1_out));  // open: cin, cout
  assign bit_extender_1_out = {{10{1'b0}}, rom_1_data[5:0]};  // Bit_Extender bit_extender_1
  ROM #(.addrWidth(16), .dataWidth(16)) rom_1 (.addr(register_1_q), .data(rom_1_data));  // open: sel
  assign bit_extender_2_out = {{4{1'b0}}, rom_1_data[11:0]};  // Bit_Extender bit_extender_2
  Multiplexer #(.width(3)) multiplexer_1 (
    .in0(rom_1_data[8:6]), .in1(rom_1_data[5:3]), .out(multiplexer_1_out), .sel(controlunit_1_regdest));  // open: en
  controlUnit controlunit_1 (
    .regDest(controlunit_1_regdest), .AluSrc(controlunit_1_alusrc), .in_1(rom_1_data[15:12]),
    .memToReg(controlunit_1_memtoreg), .regWrite(controlunit_1_regwrite), .memRead(controlunit_1_memread),
    .memWrite(controlunit_1_memwrite), .Beq(controlunit_1_beq), .BNE(controlunit_1_bne),
    .Jmp(controlunit_1_jmp), .op1(controlunit_1_op1[0]), .op2(controlunit_1_op1[1]));
  AluControl alucontrol_1 (
    .\function (rom_1_data[2:0]), .op(controlunit_1_op1), .Binvert(alucontrol_1_binvert),
    .A(alucontrol_1_b[1]), .B(alucontrol_1_b[0]));
  _16bit_register u_16bit_register_1 (
    .Read_Data_RS(n16bit_register_1_read_data_rs), .Clock(clock_1_out), .RS(rom_1_data[11:9]),
    .Read_Data_RT(n16bit_register_1_read_data_rt), .RT(rom_1_data[8:6]),
    .Write_Register_RD(multiplexer_1_out), .Write_Data(multiplexer_5_out),
    .Register_Write(controlunit_1_regwrite));
  Adder #(.width(16)) adder_2 (.a(adder_1_out), .b(bit_extender_1_out), .out(adder_2_out));  // open: cin, cout
  Multiplexer #(.width(16)) multiplexer_2 (
    .in0(n16bit_register_1_read_data_rt), .in1(bit_extender_1_out), .out(multiplexer_2_out),
    .sel(controlunit_1_alusrc));  // open: en
  _16bit_ALU u_16bit_alu_1 (
    .oparend_A(n16bit_register_1_read_data_rs), .oparend_B(multiplexer_2_out), .Operation(alucontrol_1_b),
    .B_invert(alucontrol_1_binvert), .result(n16bit_alu_1_result), .zero(n16bit_alu_1_zero),
    .Overflow(overflow), .Carry15(Carry15), .C_in(carry_in));
  Multiplexer #(.width(16)) multiplexer_3 (
    .in0(adder_1_out), .in1(adder_2_out), .out(multiplexer_3_out), .sel(or_1_out));  // open: en
  or or_1 (or_1_out, and_1_out, and_2_out);
  Multiplexer #(.width(16)) multiplexer_4 (
    .in0(multiplexer_3_out), .in1(bit_extender_2_out), .out(multiplexer_4_out), .sel(controlunit_1_jmp));  // open: en
  and and_1 (and_1_out, n16bit_alu_1_zero, controlunit_1_beq);
  not not_1 (not_1_out, n16bit_alu_1_zero);
  and and_2 (and_2_out, controlunit_1_bne, not_1_out);
  RAM #(.addrWidth(16), .dataWidth(16), .bus("separate")) ram_1 (
    .addr(n16bit_alu_1_result), .din(n16bit_register_1_read_data_rt), .data(ram_1_data),
    .str(controlunit_1_memwrite), .clk(clock_1_out), .ld(controlunit_1_memread));  // open: sel, clr
  Multiplexer #(.width(16)) multiplexer_5 (
    .in0(n16bit_alu_1_result), .in1(ram_1_data), .out(multiplexer_5_out), .sel(controlunit_1_memtoreg));  // open: en
endmodule
